# Fritzing sketch keezer (saved by Fritzing 0.9.3b)
breadboards: 1

parts:
  U1 = 4-Channel 5v Relay Shield [package=relay-4ch5v10a]
  Part1 = Adafruit I2C+SPI LCD Backpack [part_number="Adafruit #292"]
  PIR1 = PIR sensor
  Part2 = Adafruit HUZZAH ESP8266 [part_number="Adafruit #2471"]
  Mode = Square Pushbutton
  DS1 = DS18B20 1-Wire Temperature Sensor [part_number=DS18B20]
  DS2 = DS18B20 1-Wire Temperature Sensor [part_number=DS18B20]
  R1 = Resistor [tolerance=±5% resistance=4.7k package=THT]
  F1 = Fan - Ventilador [part_number="12 v DC Fan" package=THT]
  M1 = DC Motor [part_number=Compressor]
  LED1 = smd LED [color="White (4500K)" part_number="LED Strip" package="0805 [SMD]"]
  Power_plug1 = Power plug

nets (from the breadboard view):
  VCC: U1.VCC, Part1.VCC, PIR1.VDD, Part2.VBAT, LED1.cathode
  GND: U1.GND, Part1.GND, PIR1.GND, Part2.GND, F1.GND, Power_plug1.GND
  N1: U1.IN2, Part2.GPIO16
  N2: U1.K2-In, LED1.anode
  N3: U1.K2-On, U1.K3-On, Power_plug1.VCC
  N4: U1.IN4, Part2.GPIO12
  N5: U1.K3-In, F1.5V
  N6: U1.K4-On, M1.pin_2
  N7: U1.IN3, Part2.GPIO15
  N8: Part1.CLOCK, Part2.GPIO5
  N9: Part1.DATA, Part2.GPIO4
  N10: PIR1.SIG, Part2.GPIO14
  N11: Part2.GPIO13, Mode.leg0
  VDD: Part2.3.3V, DS1.VDD, DS2.VDD, R1.Pin_0
  N12: Part2.GPIO2, DS1.DQ, DS2.DQ, R1.Pin_1
  GND_2: Mode.leg1, DS1.GND, DS2.GND

notes:
  120 V AC Hot
  120v AC White
  12 V DC

custom parts:
  4-Channel 5v Relay Shield: 4 Channel 5v Relay Shield w. 2x SPD-06VDC-SD-C
  Adafruit I2C+SPI LCD Backpack: LCD backpacks reduce the number of pins needed to connect to an LCD. LCDs are a fun and easy way to have your microcontroller project talk back to you. Character LCDs are common, and easy to get, available in tons of colors and sizes. We've written tutorials on using character LCDs with an Arduino (or similar microcontroller) but find that the number of pins necessary to control the LCD can be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
  Adafruit HUZZAH ESP8266: Add Internet to your next project with an adorable, bite-sized WiFi microcontroller, at a price you like! The ESP8266 processor from Espressif is an 80 MHz microcontroller with a full WiFi front-end (both as client and access point) and TCP/IP stack with DNS support as well. While this chip has been very popular, its also been very difficult to use. Most of the low cost modules are not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
  Fan - Ventilador: Ventilador de 2 pines, se encuentra comunmente en computadoras de escritorio
